// Logisim project AndGate.circ as structural Verilog: 1 circuit, main circuit main
module main (
  input  Input1,
  input  Input2,
  output Output1
);

  and and_1 (Output1, Input1, Input2);
endmodule
