// Logisim project BitWidth.circ as structural Verilog: 1 circuit, main circuit main
module main (
  input  [3:0] Input1,
  input  [3:0] Input2,
  output [3:0] Output1
);

  assign Output1 = Input1 & Input2;  // AND_Gate and_1, 4 bits wide
endmodule
