// Logisim project Gates1.circ as structural Verilog: 4 circuits, main circuit main
module main (
  input  Input1,
  input  Input2,
  output Output1
);

  and and_1 (Output1, Input1, Input2);
endmodule

module ORGate (
  input  Input1,
  input  Input2,
  output Output1
);

  or or_1 (Output1, Input1, Input2);
endmodule

module AndGate2 (
  input  Input1,
  input  Input2,
  output Output1
);

  and and_1 (Output1, Input1, Input2);
endmodule

module XORGate (
  input  Input1,
  input  Input2,
  output Output1
);

  xor xor_1 (Output1, Input1, Input2);
endmodule
