// Logisim project Gates2.circ as structural Verilog: 6 circuits, main circuit main
module main (
  input  Input1,
  input  Input2,
  output Output1
);

  wire Not_output1;

  NOTGate Not (.Input1(Input2), .Output1(Not_output1));
  and and_1 (Output1, Input1, Not_output1);
endmodule

module NANDGate (
  input  Input1,
  input  Input2,
  output Output1
);

  nand nand_1 (Output1, Input1, Input2);
endmodule

module NORGate (
  input  Input1,
  input  Input2,
  output Output1
);

  nor nor_1 (Output1, Input1, Input2);
endmodule

module NOTGate (
  input  Input1,
  output Output1
);

  not not_1 (Output1, Input1);
endmodule

module BufferGate (
  input  Input1,
  output Output1
);

  buf buffer_1 (Output1, Input1);
endmodule

module XNORGate (
  input  Input1,
  input  Input2,
  output Output1
);

  xnor xnor_1 (Output1, Input1, Input2);
endmodule
