// Logisim project Gates3.circ as structural Verilog: 6 circuits, main circuit main
module main (
  input  Input1,
  input  Input2,
  input  Input3,
  output Output1,
  output Output2,
  output Output3
);

  wire Not_output1;

  NOTGate Not (.Input1(Input2), .Output1(Not_output1));
  and and_1 (Output1, Input1, Not_output1);
  NANDGate nandgate_1 (.Input1(Input3), .Input2(Input3), .Input3(Input3), .Output1(Output2), .Output2(Output3));
endmodule

module NANDGate (
  input  Input1,
  input  Input2,
  input  Input3,
  output Output1,
  output Output2
);

  NOTGate notgate_1 (.Input1(Input3), .Output1(Output2));
  nand nand_1 (Output1, Input1, Input2);
endmodule

module NORGate (
  input  Input1,
  input  Input2,
  output Output1
);

  nor nor_1 (Output1, Input1, Input2);
endmodule

module NOTGate (
  input  Input1,
  output Output1
);

  not not_1 (Output1, Input1);
endmodule

module BufferGate (
  input  Input1,
  output Output1
);

  buf buffer_1 (Output1, Input1);
endmodule

module XNORGate (
  input  Input1,
  input  Input2,
  output Output1
);

  xnor xnor_1 (Output1, Input1, Input2);
endmodule
