// Logisim project Gates_Simple.circ as structural Verilog
module And_Gate (
  input  Input1,
  input  Input2,
  output Output1
);

  and and_1 (Output1, Input1, Input2);
endmodule

module And_Gate_2 (
  input  Input1,
  input  Input2,
  output Output1
);

  and and_1 (Output1, Input1, Input2);
endmodule

module OR_Gate (
  input  Input1,
  input  Input2,
  output Output1
);

  or or_1 (Output1, Input1, Input2);
endmodule

module NAND_Gate (
  input  Input1,
  input  Input2,
  output Output1
);

  nand nand_1 (Output1, Input1, Input2);
endmodule

module NOR_Gate (
  input  Input1,
  input  Input2,
  output Output1
);

  nor nor_1 (Output1, Input1, Input2);
endmodule

module NOT_Gate (
  input  Input1,
  output Output1
);

  not not_1 (Output1, Input1);
endmodule

module Buffer_Gate (
  input  Input1,
  output Output1
);

  buf buffer_1 (Output1, Input1);
endmodule

module XOR_Gate (
  input  Input1,
  input  Input2,
  output Output1
);

  xor xor_1 (Output1, Input1, Input2);
endmodule

module XNOR_Gate (
  input  Input1,
  input  Input2,
  output Output1
);

  xnor xnor_1 (Output1, Input1, Input2);
endmodule
