// Logisim project Plexers.circ as structural Verilog: 6 circuits, main circuit mux
module mux (
  input  Input1,
  input  Input2,
  input  Control,
  input  Enable,
  output Output1
);

  Multiplexer multiplexer_1 (.in0(Input1), .in1(Input2), .out(Output1), .sel(Control), .en(Enable));
endmodule

module demux (
  input  Input1,
  input  Enable,
  input  Control,
  output Output1,
  output Output2
);

  Demultiplexer demultiplexer_1 (.out0(Output1), .out1(Output2), .in(Input1), .sel(Control), .en(Enable));
endmodule

module decod (
  input  Enable,
  input  Select,
  output Output1,
  output Output2
);

  Decoder decoder_1 (.out0(Output1), .out1(Output2), .sel(Select), .en(Enable));
endmodule

module encod (
  input  Input1,
  input  Input2,
  input  IEnable,
  output out_4,
  output Output1,
  output OGroup
);

  Priority_Encoder #(.select(1)) priority_encoder_1 (
    .in0(Input1), .in1(Input2), .out(Output1), .gs(OGroup), .en_out(out_4), .en_in(IEnable));
endmodule

module bselect (
  input  [7:0] Input1,
  input  [2:0] Select,
  output Outpu1
);

  BitSelector bitselector_1 (.in(Input1), .out(Outpu1), .sel(Select));
endmodule

module testing_wires (
  input  Input1,
  input  Input2,
  input  mSig,
  input  dEanble,
  input  mEnable,
  input  dSig,
  output Output1,
  output Output2
);

  wire multiplexer_1_out;

  Multiplexer multiplexer_1 (.in0(Input1), .in1(Input2), .out(multiplexer_1_out), .sel(mSig), .en(mEnable));
  Demultiplexer demultiplexer_1 (.out0(Output1), .out1(Output2), .in(multiplexer_1_out), .sel(dSig), .en(dEanble));
endmodule
