// Logisim project PowerGroundConst.circ as structural Verilog: 1 circuit, main circuit main
module main (
  output Output1,
  output Output2,
  output Output3,
  output Output4,
  output Output5,
  output Output6
);

  not Not1 (Output3, 1'b1);
  not Not2 (Output4, 1'b0);
  not Not3 (Output6, 1'b1);

  assign Output1 = 1'b1;
  assign Output2 = 1'b0;
  assign Output5 = 1'b0;
endmodule
