// Logisim project Splitter.circ as structural Verilog: 1 circuit, main circuit main
module main (
  input  [3:0] Input1,
  output Output1,
  output Output2,
  output Output3
);

  and and_1 (Output1, Input1[0], Input1[0], Input1[1]);
  not not_1 (Output2, Input1[2]);

  assign Output3 = Input1[3];
endmodule
